# Fritzing sketch proj (saved by Fritzing 0.9.2b)

parts:
  Часть1 = Arduino Nano (Rev3.0)
  DFPlayer_Mini1 = DFPlayer MINI [package="DIP (Dual Inline) [THT]"]
  S1 = Momentary Switch [package=ksa_sealed_tac_switch]
  S2 = Momentary Switch [package=ksa_sealed_tac_switch]
  S3 = Momentary Switch [package=ksa_sealed_tac_switch]
  PCB2 = RTC_DS1302_module
  S4 = Momentary Switch [package=ksa_sealed_tac_switch]

nets:
  GND: Часть1.GND, DFPlayer_Mini1.GND, S4.1
  N1: Часть1.D2, DFPlayer_Mini1.TX
  N2: Часть1.D3, DFPlayer_Mini1.RX
  N3: Часть1.D4, S4.3
  N4: Часть1.D5, S3.2
  N5: Часть1.D6, S2.2
  N6: Часть1.D7, S1.2
  N7: Часть1.D8, PCB2.RST
  N8: Часть1.D9, PCB2.DAT
  N9: Часть1.D10, PCB2.CLK
  5V: Часть1.5V, DFPlayer_Mini1.VCC
  N10: Часть1.A0, DFPlayer_Mini1.BUSY

custom parts:
  DFPlayer MINI: MP3 module by DFRobot.com for playing Music from an SD-Card. Supports WAV and MP3 files.
  RTC_DS1302_module: Arduino module DS1302 SPI Real Time Clock
